# Fritzing sketch cube (saved by Fritzing 0.6.3b)
breadboards: 2

parts:
  Arduino1 = Arduino
  U1 = 74HC595 [package="DIP16 [THT]"]
  U2 = 74HC595 [package="DIP16 [THT]"]
  U3 = 74HC595 [package="DIP16 [THT]"]
  S1 = Round Pushbutton
  R1 = Resistor [tolerance=±5% resistance=220 package=THT]
  R6 = Rotary Potentiometer (Large) [maximum_resistance=100kΩ package=THT]
  R7 = Rotary Potentiometer (Large) [maximum_resistance=100kΩ package=THT]
  R8 = Rotary Potentiometer (Large) [maximum_resistance=100kΩ package=THT]
  R9 = Resistor [tolerance=±5% resistance=220 package=THT]
  R10 = Resistor [tolerance=±5% resistance=220 package=THT]
  R11 = Resistor [tolerance=±5% resistance=220 package=THT]
  R12 = Resistor [tolerance=±5% resistance=220 package=THT]
  R13 = Resistor [tolerance=±5% resistance=220 package=THT]
  R14 = Resistor [tolerance=±5% resistance=220 package=THT]
  R15 = Resistor [tolerance=±5% resistance=220 package=THT]
  R16 = Resistor [tolerance=±5% resistance=220 package=THT]
  R17 = Resistor [tolerance=±5% resistance=220 package=THT]
  LED29 = smd LED [color="Red (633nm)" package="0603 [SMD]"]
  LED31 = smd LED [color="Red (633nm)" package="0603 [SMD]"]
  LED36 = smd LED [color="Red (633nm)" package="0603 [SMD]"]
  LED37 = smd LED [color="Red (633nm)" package="0603 [SMD]"]
  LED38 = smd LED [color="Red (633nm)" package="0603 [SMD]"]
  LED39 = smd LED [color="Red (633nm)" package="0603 [SMD]"]
  LED40 = smd LED [color="Red (633nm)" package="0603 [SMD]"]
  LED41 = smd LED [color="Red (633nm)" package="0603 [SMD]"]
  LED42 = smd LED [color="Red (633nm)" package="0603 [SMD]"]
  LED43 = smd LED [color="Red (633nm)" package="0603 [SMD]"]
  LED44 = smd LED [color="Red (633nm)" package="0603 [SMD]"]
  LED45 = smd LED [color="Red (633nm)" package="0603 [SMD]"]
  LED46 = smd LED [color="Red (633nm)" package="0603 [SMD]"]
  LED47 = smd LED [color="Red (633nm)" package="0603 [SMD]"]
  LED48 = smd LED [color="Red (633nm)" package="0603 [SMD]"]
  LED49 = smd LED [color="Red (633nm)" package="0603 [SMD]"]
  LED50 = smd LED [color="Red (633nm)" package="0603 [SMD]"]
  LED51 = smd LED [color="Red (633nm)" package="0603 [SMD]"]
  LED52 = smd LED [color="Red (633nm)" package="0603 [SMD]"]
  LED53 = smd LED [color="Red (633nm)" package="0603 [SMD]"]
  LED54 = smd LED [color="Red (633nm)" package="0603 [SMD]"]
  LED55 = smd LED [color="Red (633nm)" package="0603 [SMD]"]
  LED56 = smd LED [color="Red (633nm)" package="0603 [SMD]"]
  LED57 = smd LED [color="Red (633nm)" package="0603 [SMD]"]
  LED58 = smd LED [color="Red (633nm)" package="0603 [SMD]"]
  LED59 = smd LED [color="Red (633nm)" package="0603 [SMD]"]
  LED60 = smd LED [color="Red (633nm)" package="0603 [SMD]"]
  Q1 = NPN-Transistor [package="TO92 [THT]"]
  Q2 = NPN-Transistor [package="TO92 [THT]"]
  Q3 = NPN-Transistor [package="TO92 [THT]"]
  R18 = Resistor [tolerance=±5% resistance=220 package=THT]
  R19 = Resistor [tolerance=±5% resistance=220 package=THT]
  R20 = Resistor [tolerance=±5% resistance=220 package=THT]

nets:
  GND: Arduino1.GND, U1.GND, U1.OE, U2.GND, U2.OE, U3.GND, U3.OE, R17.Pin_0, Q1.C, Q2.C, Q3.C
  N1: Arduino1.D12, S1.leg0, R17.Pin_1
  N2: Arduino1.D10, U3.SH_CP
  N3: Arduino1.D9, U3.ST_CP
  N4: Arduino1.D8, U3.DS
  N5: Arduino1.D4, U1.SH_CP, U2.SH_CP
  N6: Arduino1.D3, U1.ST_CP, U2.ST_CP
  N7: Arduino1.D2, U1.DS
  VCC: Arduino1.+5V, U1.MR, U1.VCC, U2.MR, U2.VCC, U3.MR, U3.VCC, S1.leg1
  N8: Arduino1.A0, R8.wiper
  N9: Arduino1.A2, R7.wiper
  N10: Arduino1.A4, R6.wiper
  N11: U1.Q1, R9.Pin_0
  N12: U1.Q2, R10.Pin_0
  N13: U1.Q3, R11.Pin_0
  N14: U1.Q4, R12.Pin_0
  N15: U1.Q5, R13.Pin_0
  N16: U1.Q6, R14.Pin_0
  N17: U1.Q7, R15.Pin_0
  N18: U1.Q7', U2.DS
  N19: U1.Q0, R1.Pin_0
  N20: U2.Q0, R16.Pin_0
  N21: U3.Q1, R20.Pin_1
  N22: U3.Q2, R19.Pin_1
  N23: U3.Q0, R18.Pin_1
  N24: R1.Pin_1, LED29.anode, LED43.anode, LED52.anode
  N25: R6.leg1, R7.leg1, R8.leg1
  N26: R6.leg2, R7.leg2, R8.leg2
  N27: R9.Pin_1, LED36.anode, LED48.anode, LED57.anode
  N28: R10.Pin_1, LED31.anode, LED44.anode, LED53.anode
  N29: R11.Pin_1, LED37.anode, LED45.anode, LED54.anode
  N30: R12.Pin_1, LED39.anode, LED47.anode, LED56.anode
  N31: R13.Pin_1, LED38.anode, LED46.anode, LED55.anode
  N32: R14.Pin_1, LED49.anode
  N33: R15.Pin_1, LED42.anode, LED51.anode, LED60.anode
  N34: R16.Pin_1, LED41.anode, LED50.anode, LED59.anode
  N35: LED29.cathode, LED31.cathode, LED36.cathode, LED37.cathode, LED38.cathode, LED39.cathode, LED40.cathode, LED41.cathode, LED42.cathode, Q2.E
  N36: LED40.anode, LED58.anode
  N37: LED43.cathode, LED44.cathode, LED45.cathode, LED46.cathode, LED47.cathode, LED48.cathode, LED49.cathode, LED50.cathode, LED51.cathode, Q3.E
  N38: LED52.cathode, LED53.cathode, LED54.cathode, LED55.cathode, LED56.cathode, LED57.cathode, LED58.cathode, LED59.cathode, LED60.cathode, Q1.E
  N39: Q1.B, R18.Pin_0
  N40: Q2.B, R20.Pin_0
  N41: Q3.B, R19.Pin_0
